// Logisim project BOB-2200.circ as structural Verilog: 3 circuits, main circuit my circuit
module my_circuit (
  output [3:0] out_1
);

  wire CLK, CLR, comparator_1_eq, comparator_1_lt, CondType, DrALU, DrCmp, DrMEM, DrOFF, DrPC, DrReg, LdA,
       LdB, LdCmp, LdIR, LdMAR, LdPC, multiplexer_1_out, not_1_out, WrMEM, WrREG;
  wire [0:0] CmpReg_q;
  wire [1:0] func, RegSel;
  wire [3:0] OPCODE, RX, RY, RZ;
  wire [5:0] multiplexer_2_out, rom_1_data, rom_2_data, State_Register_q;
  wire [19:4] IR_q;
  wire [24:0] rom_3_data;
  wire [31:0] A_q, B_q, bit_extender_1_out, bit_extender_2_out, controlled_buffer_1_out, MAR_q,
       n32_bit_alu_1_out_4, PC_q, ram_1_data, regfile_1_out_6;

  Register #(.width(32)) PC (.D(controlled_buffer_1_out), .en(LdPC), .Q(PC_q), .clk(CLK), .clr(CLR));
  assign controlled_buffer_1_out = DrPC ? PC_q : 32'bz;  // Controlled_Buffer controlled_buffer_1
  Comparator #(.width(32)) comparator_1 (
    .a(controlled_buffer_1_out), .b({32{1'b0}}), .eq(comparator_1_eq), .lt(comparator_1_lt));  // open: gt
  not not_1 (not_1_out, comparator_1_eq);
  Multiplexer #(.disabled(0), .enable("false")) multiplexer_1 (
    .in0(not_1_out), .in1(comparator_1_lt), .out(multiplexer_1_out), .sel(CondType));
  Register #(.width(32)) A (.D(controlled_buffer_1_out), .en(LdA), .Q(A_q), .clk(CLK), .clr(CLR));
  _32_bit_ALU u_32_bit_alu_1 (.out_4(n32_bit_alu_1_out_4), .in_2(A_q), .in_3(B_q), .in_1(func));
  assign controlled_buffer_1_out = DrALU ? n32_bit_alu_1_out_4 : 32'bz;  // Controlled_Buffer controlled_buffer_2
  Register #(.width(1)) CmpReg (.D(multiplexer_1_out), .en(LdCmp), .Q(CmpReg_q[0]), .clk(CLK), .clr(CLR));
  Clock clock_1 (.out(CLK));
  Register #(.width(32)) B (.D(controlled_buffer_1_out), .en(LdB), .Q(B_q), .clk(CLK), .clr(CLR));
  assign controlled_buffer_1_out = DrCmp ? bit_extender_1_out : 32'bz;  // Controlled_Buffer controlled_buffer_3
  assign bit_extender_1_out = {{31{1'b0}}, CmpReg_q[0]};  // Bit_Extender bit_extender_1
  Button button_1 (.out(CLR));
  RegFile regfile_1 (
    .out_6(regfile_1_out_6), .in_1(out_1), .in_5(controlled_buffer_1_out), .in_2(WrREG), .in_3(CLK),
    .in_4(CLR));
  assign controlled_buffer_1_out = DrReg ? regfile_1_out_6 : 32'bz;  // Controlled_Buffer controlled_buffer_4
  Register #(.width(32)) MAR (.D(controlled_buffer_1_out), .en(LdMAR), .Q(MAR_q), .clk(CLK), .clr(CLR));
  ROM #(.addrWidth(4), .dataWidth(6)) rom_1 (.addr(OPCODE), .data(rom_1_data));  // open: sel
  ROM #(.addrWidth(2), .dataWidth(6)) rom_2 (.addr({1'b0, CmpReg_q[0]}), .data(rom_2_data));  // open: sel
  RAM #(.addrWidth(24), .dataWidth(32), .bus("separate")) ram_1 (
    .addr(MAR_q[23:0]), .din(controlled_buffer_1_out), .data(ram_1_data), .str(WrMEM), .clk(CLK));  // open: sel, ld, clr
  assign controlled_buffer_1_out = DrMEM ? ram_1_data : 32'bz;  // Controlled_Buffer controlled_buffer_5
  Multiplexer #(.select(2), .width(6), .disabled(0), .enable("false")) multiplexer_2 (
    .in0(rom_3_data[5:0]), .in1(rom_1_data), .in2(rom_2_data), .out(multiplexer_2_out),
    .sel(rom_3_data[24:23]));  // open: in3
  Register #(.width(32)) IR (
    .D(controlled_buffer_1_out), .en(LdIR), .Q({OPCODE, RX, RY, IR_q, RZ}), .clk(CLK), .clr(CLR));
  Register #(.width(6)) State_Register (.D(multiplexer_2_out), .Q(State_Register_q), .clk(CLK), .clr(CLR));  // open: en
  assign bit_extender_2_out = {{12{IR_q[19]}}, {IR_q, RZ}};  // Bit_Extender bit_extender_2
  assign controlled_buffer_1_out = DrOFF ? bit_extender_2_out : 32'bz;  // Controlled_Buffer controlled_buffer_6
  ROM #(.addrWidth(6), .dataWidth(27)) rom_3 (
    .addr(State_Register_q),
    .data({CondType, DrCmp, rom_3_data[24:23], func, RegSel, WrMEM, WrREG, LdCmp, LdB, LdA, LdMAR, LdIR, LdPC, DrOFF, DrPC, DrALU, DrMEM, DrReg, rom_3_data[5:0]}));  // open: sel
  Multiplexer #(.select(2), .width(4), .disabled(0), .enable("false")) multiplexer_3 (
    .in0(RX), .in1(RY), .in2(RZ), .out(out_1), .sel(RegSel));  // open: in3

  // Other names for the same wires on the sheet: regno[3:0] = out_1

  // Notes on the sheet:
  //   ALU
  //   RegFile
  //   SeqROM
  //   CondROM
  //   Memory
  //   contents of rom_1 (hex, n*v repeats v):
  //   3 6 9 c 10 14 1b 1d 1e 22
  //   contents of rom_2 (hex, n*v repeats v):
  //   0 18
  //   OPTEST
  //   ChkCmp
  //   MainROM
  //   contents of rom_3 (hex, n*v repeats v):
  //   6201 1082 e00900 84044 108045 20100 84047 108048 420100 8404a 840b 20100 8404d 840e 210f 20080 84051
  //   8412 2113 40040 4055 88056 210117 1000018 4219 841a 900 2021c 80840 1d 8405f 108060 4210121 2020000
  //   4223 8424 20100
endmodule

module RegFile (
  input  [3:0] in_1,
  input  in_2,
  input  in_3,
  input  in_4,
  input  [31:0] in_5,
  output [31:0] out_6
);

  wire and_1_out, and_2_out, and_3_out, and_4_out, and_5_out, and_6_out, and_7_out, and_8_out, and_9_out,
       and_10_out, and_11_out, and_12_out, and_13_out, and_14_out, and_15_out, and_16_out, decoder_1_out0,
       decoder_1_out1, decoder_1_out2, decoder_1_out3, decoder_1_out4, decoder_1_out5, decoder_1_out6,
       decoder_1_out7, decoder_1_out8, decoder_1_out9, decoder_1_out10, decoder_1_out11, decoder_1_out12,
       decoder_1_out13, decoder_1_out14, decoder_1_out15;
  wire [31:0] a0, a1, a2, at, fp, k0, ra, s0, s1, s2, sp, t0, t1, t2, v0, zero;

  Decoder #(.select(4), .enable("false")) decoder_1 (
    .out0(decoder_1_out0), .out1(decoder_1_out1), .out2(decoder_1_out2), .out3(decoder_1_out3),
    .out4(decoder_1_out4), .out5(decoder_1_out5), .out6(decoder_1_out6), .out7(decoder_1_out7),
    .out8(decoder_1_out8), .out9(decoder_1_out9), .out10(decoder_1_out10), .out11(decoder_1_out11),
    .out12(decoder_1_out12), .out13(decoder_1_out13), .out14(decoder_1_out14), .out15(decoder_1_out15),
    .sel(in_1));
  Register #(.width(32)) u_zero (.D({32{1'b0}}), .en(and_1_out), .Q(zero), .clk(in_3), .clr(1'b1));
  and and_1 (and_1_out, decoder_1_out0, in_2);
  Register #(.width(32)) u_at (.D(in_5), .en(and_2_out), .Q(at), .clk(in_3), .clr(in_4));
  and and_2 (and_2_out, decoder_1_out1, in_2);
  Register #(.width(32)) u_v0 (.D(in_5), .en(and_3_out), .Q(v0), .clk(in_3), .clr(in_4));
  and and_3 (and_3_out, decoder_1_out2, in_2);
  Register #(.width(32)) u_a0 (.D(in_5), .en(and_4_out), .Q(a0), .clk(in_3), .clr(in_4));
  and and_4 (and_4_out, decoder_1_out3, in_2);
  Register #(.width(32)) u_a1 (.D(in_5), .en(and_5_out), .Q(a1), .clk(in_3), .clr(in_4));
  and and_5 (and_5_out, decoder_1_out4, in_2);
  Register #(.width(32)) u_a2 (.D(in_5), .en(and_6_out), .Q(a2), .clk(in_3), .clr(in_4));
  and and_6 (and_6_out, decoder_1_out5, in_2);
  Register #(.width(32)) u_t0 (.D(in_5), .en(and_7_out), .Q(t0), .clk(in_3), .clr(in_4));
  and and_7 (and_7_out, decoder_1_out6, in_2);
  Register #(.width(32)) u_t1 (.D(in_5), .en(and_8_out), .Q(t1), .clk(in_3), .clr(in_4));
  and and_8 (and_8_out, decoder_1_out7, in_2);
  Register #(.width(32)) u_t2 (.D(in_5), .en(and_9_out), .Q(t2), .clk(in_3), .clr(in_4));
  and and_9 (and_9_out, decoder_1_out8, in_2);
  Register #(.width(32)) u_s0 (.D(in_5), .en(and_10_out), .Q(s0), .clk(in_3), .clr(in_4));
  and and_10 (and_10_out, decoder_1_out9, in_2);
  Register #(.width(32)) u_s1 (.D(in_5), .en(and_11_out), .Q(s1), .clk(in_3), .clr(in_4));
  and and_11 (and_11_out, decoder_1_out10, in_2);
  Register #(.width(32)) u_s2 (.D(in_5), .en(and_12_out), .Q(s2), .clk(in_3), .clr(in_4));
  and and_12 (and_12_out, decoder_1_out11, in_2);
  Register #(.width(32)) u_k0 (.D(in_5), .en(and_13_out), .Q(k0), .clk(in_3), .clr(in_4));
  and and_13 (and_13_out, decoder_1_out12, in_2);
  Register #(.width(32)) u_sp (.D(in_5), .en(and_14_out), .Q(sp), .clk(in_3), .clr(in_4));
  and and_14 (and_14_out, decoder_1_out13, in_2);
  Register #(.width(32)) u_fp (.D(in_5), .en(and_15_out), .Q(fp), .clk(in_3), .clr(in_4));
  and and_15 (and_15_out, decoder_1_out14, in_2);
  Register #(.width(32)) u_ra (.D(in_5), .en(and_16_out), .Q(ra), .clk(in_3), .clr(in_4));
  and and_16 (and_16_out, decoder_1_out15, in_2);
  Multiplexer #(.select(4), .width(32), .enable("false")) multiplexer_1 (
    .in0(zero), .in1(at), .in2(v0), .in3(a0), .in4(a1), .in5(a2), .in6(t0), .in7(t1), .in8(t2), .in9(s0),
    .in10(s1), .in11(s2), .in12(k0), .in13(sp), .in14(fp), .in15(ra), .out(out_6), .sel(in_1));

  // Other names for the same wires on the sheet: CLK = in_3; CLR = in_4; Din[31:0] = in_5; regno[3:0] = in_1;
  //   WrREG = in_2
endmodule

module _32_bit_ALU (
  input  [1:0] in_1,
  input  [31:0] in_2,
  input  [31:0] in_3,
  output [31:0] out_4
);

  wire [31:0] adder_1_out, adder_2_out, nand_1_out, subtractor_1_out;

  Adder #(.width(32)) adder_1 (.a(in_2), .b(in_3), .out(adder_1_out));  // open: cin, cout
  Subtractor #(.width(32)) subtractor_1 (.a(in_2), .b(in_3), .out(subtractor_1_out));  // open: bin, bout
  assign nand_1_out = ~(in_2 & in_3);  // NAND_Gate nand_1, 32 bits wide
  Adder #(.width(32)) adder_2 (.a(in_2), .b(32'h1), .out(adder_2_out));  // open: cin, cout
  Multiplexer #(.select(2), .width(32), .disabled(0), .enable("false")) multiplexer_1 (
    .in0(adder_1_out), .in1(subtractor_1_out), .in2(nand_1_out), .in3(adder_2_out), .out(out_4), .sel(in_1));

  // Other names for the same wires on the sheet: A[31:0] = in_2; B[31:0] = in_3; func[1:0] = in_1

  // Notes on the sheet:
  //   A + B
  //   A - B
  //   A + 1
endmodule
