// Logisim project project2-devices.circ as structural Verilog: 1 circuit, main circuit Timer Device
module Timer_Device (
  input  Clock,
  input  IntAck_In,
  input  [31:0] Limit,
  input  [31:0] ID,
  output Int,
  output [31:0] Data,
  output IntAck_Out
);

  wire and_3_out, button_1_out, comparator_1_eq, comparator_1_gt, IntAck, IntRaise, not_1_out, or_1_out,
       PushID;
  wire [31:0] Timer_q;

  assign IntAck = IntAck_In ? 1'b1 : 1'bz;  // Controlled_Buffer controlled_buffer_1
  Pull_Resistor pull_resistor_1 (.node(IntAck));
  and and_1 (PushID, IntRaise, IntAck);
  assign Int = IntRaise ? 1'b1 : 1'bz;  // Controlled_Buffer controlled_buffer_2
  and and_2 (IntAck_Out, IntAck, ~IntRaise);  // AND_Gate
  not not_1 (not_1_out, IntAck);
  Counter #(.width(32), .max('hffffffff), .ongoal("stay")) Timer (
    .load(IntAck), .D({32{1'b0}}), .count(not_1_out), .Q(Timer_q), .clk(Clock), .clr(button_1_out));  // open: carry
  Button button_1 (.out(button_1_out));
  assign Data = PushID ? ID : 32'bz;  // Controlled_Buffer controlled_buffer_3
  or or_1 (or_1_out, comparator_1_gt, comparator_1_eq);
  Comparator #(.width(32), .mode("unsigned")) comparator_1 (
    .a(Timer_q), .b(Limit), .gt(comparator_1_gt), .eq(comparator_1_eq));  // open: lt
  and and_3 (and_3_out, or_1_out, ~IntAck);  // AND_Gate
  D_Flip_Flop d_ff_1 (.clk(Clock), .D(and_3_out), .Q(IntRaise));  // open: Qn, preset, en, reset

  // Other names for the same wires on the sheet: DeviceID[31:0] = ID

  // Notes on the sheet:
  //   Clear Button
endmodule
