// Logisim project BOB2200-pipeline.circ as structural Verilog: 8 circuits, main circuit main
module main (
);

  wire and_1_out, and_2_out, CLK, comparator_1_eq, comparator_2_eq, comparator_3_eq, comparator_4_eq,
       comparator_5_eq, comparator_6_eq, comparator_7_eq, comparator_9_eq, comparator_11_eq, if_JALR, if_LEA,
       if_LW, multiplexer_2_out, NOP, not_1_out, not_2_out, not_3_out, not_4_out, not_5_out, not_6_out,
       OffsetEn, RxDR, RxSR, RySR, RzSR, STALL, WREn;
  wire [1:0] A_Selector, B_Selector, func, or_4_out, PC_Input_selector;
  wire [3:0] bit_extender_1_out, bit_extender_2_out, controlled_buffer_3_out, if_idrr_buffer_1_opcode,
       if_idrr_buffer_1_rz, multiplexer_3_out, multiplexer_4_out, multiplexer_5_out, OPCODE_EX, OPCODE_MEM,
       OPCODE_WB, Rx, Ry, Rz;
  wire [19:0] if_idrr_buffer_1_offset;
  wire [23:0] bit_extender_5_out;
  wire [31:0] adder_3_out, ALU_Result, ALU_Result_MEM, ALU_RESULT_WB, bit_extender_3_out, bit_extender_4_out,
       controlled_buffer_2_out, controlled_buffer_4_out, D_Mem_Out, D_Mem_Out_WB, DPRF_Input, DPRF_Output1,
       DPRF_Output2, if_idrr_buffer_1_inc_pc_reg, Inc_PC_MEM, Inc_PC_Reg_EX, Inc_PC_WB, multiplexer_1_out,
       multiplexer_6_out, multiplexer_7_out, multiplexer_8_out, multiplexer_9_out, multiplexer_10_out,
       multiplexer_11_out, Offset_EX, Offset_MEM, Offset_WB, PC___Offset_Ex, PC_q, pull_resistor_3_node,
       ram_1_data, Rx_Reg_EX, Rx_Reg_MEM, Rx_Reg_WB, Ry_Reg_EX, Ry_Reg_MEM, Ry_Reg_WB, Rz_Reg_EX, Rz_Reg_MEM;

  Pull_Resistor pull_resistor_1 (.node(STALL));
  Clock clock_1 (.out(CLK));
  or or_1 (NOP, PC_Input_selector[0], PC_Input_selector[1]);
  Multiplexer #(.select(2), .width(32), .disabled(0), .enable("false")) multiplexer_1 (
    .in0(pull_resistor_3_node), .in1(PC___Offset_Ex), .in2(Ry_Reg_EX), .in3(Inc_PC_Reg_EX),
    .out(multiplexer_1_out), .sel(PC_Input_selector));
  Multiplexer #(.disabled(0), .enable("false")) multiplexer_2 (
    .in0(1'b1), .in1(1'b0), .out(multiplexer_2_out), .sel(STALL));
  Pull_Resistor pull_resistor_2 (.node(PC_Input_selector));
  Register #(.width(32)) PC (.D(multiplexer_1_out), .en(multiplexer_2_out), .Q(PC_q), .clk(CLK));  // open: clr
  Pull_Resistor pull_resistor_3 (.node(pull_resistor_3_node));
  Adder #(.width(32)) adder_1 (.a(PC_q), .b(32'h1), .out(pull_resistor_3_node));  // open: cin, cout
  Stall_Handler stall_handler_1 (
    .OPCODE_EX(OPCODE_EX), .OPCODE_MEM(OPCODE_MEM), .OPCODE_WB(OPCODE_WB), .DPRF_IN0(multiplexer_4_out),
    .DPRF_IN2(multiplexer_5_out), .RX_EX(Rx_Reg_EX), .RX_MEM(Rx_Reg_MEM), .RX_WB(Rx_Reg_WB), .STALL(STALL));
  RAM #(.addrWidth(24), .dataWidth(32)) ram_1 (.addr(PC_q[23:0]), .data(ram_1_data), .clk(CLK));  // open: sel, ld, clr
  not not_1 (not_1_out, OffsetEn);
  assign Rz = not_1_out ? if_idrr_buffer_1_rz : 4'bz;  // Controlled_Buffer controlled_buffer_1
  IF_IDRR_Buffer if_idrr_buffer_1 (
    .in_1(CLK), .I_MEM_out(ram_1_data), .Inc_PC(pull_resistor_3_node), .in_2(NOP), .in_3(STALL),
    .Offset(if_idrr_buffer_1_offset), .Rz(if_idrr_buffer_1_rz), .Ry(Ry), .Rx(Rx),
    .OPCODE(if_idrr_buffer_1_opcode), .Inc_PC_Reg(if_idrr_buffer_1_inc_pc_reg));
  Bit_Extender #(.in_width(32), .out_width(4), .\type ("sign")) bit_extender_1 (
    .in(Rx_Reg_WB), .out(bit_extender_1_out));
  Bit_Extender #(.in_width(32), .out_width(4), .\type ("sign")) bit_extender_2 (
    .in(Ry_Reg_WB), .out(bit_extender_2_out));
  assign bit_extender_3_out = {{12{if_idrr_buffer_1_offset[19]}}, if_idrr_buffer_1_offset};  // Bit_Extender bit_extender_3
  Pull_Resistor pull_resistor_4 (.node(Rz));
  Multiplexer #(.width(4), .disabled(0), .enable("false")) multiplexer_3 (
    .in0(bit_extender_1_out), .in1(bit_extender_2_out), .out(multiplexer_3_out), .sel(if_JALR));
  assign controlled_buffer_2_out = OffsetEn ? bit_extender_3_out : 32'bz;  // Controlled_Buffer controlled_buffer_2
  assign controlled_buffer_3_out = RxDR ? Rx : 4'bz;  // Controlled_Buffer controlled_buffer_3
  Multiplexer #(.width(4), .disabled(0), .enable("false")) multiplexer_4 (
    .in0(Ry), .in1(Rx), .out(multiplexer_4_out), .sel(RxSR));
  Multiplexer #(.width(4), .disabled(0), .enable("false")) multiplexer_5 (
    .in0(Rz), .in1(Ry), .out(multiplexer_5_out), .sel(RxSR));
  assign bit_extender_4_out = {{28{controlled_buffer_3_out[3]}}, controlled_buffer_3_out};  // Bit_Extender bit_extender_4
  Multiplexer #(.width(32), .disabled(0), .enable("false")) multiplexer_6 (
    .in0(bit_extender_4_out), .in1(DPRF_Output1), .out(multiplexer_6_out), .sel(RxSR));
  Multiplexer #(.width(32), .disabled(0), .enable("false")) multiplexer_7 (
    .in0(DPRF_Output1), .in1(DPRF_Output2), .out(multiplexer_7_out), .sel(RxSR));
  ROM #(.addrWidth(4), .dataWidth(5)) rom_1 (
    .addr(if_idrr_buffer_1_opcode), .data({OffsetEn, RzSR, RySR, RxSR, RxDR}));  // open: sel
  Pull_Resistor pull_resistor_5 (.node(multiplexer_6_out));
  Pull_Resistor pull_resistor_6 (.node(multiplexer_7_out));
  Dual_Ported_Register_File dual_ported_register_file_1 (
    .CLK(CLK), .WrREGNO(multiplexer_3_out), .RdREGNO1(multiplexer_4_out), .RdREGNO2(multiplexer_5_out),
    .INPUT(DPRF_Input), .OUT1(DPRF_Output1), .OUT2(DPRF_Output2), .WrEN(WREn));
  Pull_Resistor pull_resistor_7 (.node(controlled_buffer_2_out));
  assign controlled_buffer_4_out = not_2_out ? DPRF_Output2 : 32'bz;  // Controlled_Buffer controlled_buffer_4
  not not_2 (not_2_out, RxSR);
  IDRR_EX_Buffer idrr_ex_buffer_1 (
    .CLK(CLK), .Offset(controlled_buffer_2_out), .Rx_Reg(multiplexer_6_out), .Ry_Reg(multiplexer_7_out),
    .Rz_Reg(controlled_buffer_4_out), .OPCODE(if_idrr_buffer_1_opcode),
    .Inc_PC_Reg(if_idrr_buffer_1_inc_pc_reg), .in_2(NOP), .in_3(STALL), .Offset_Reg(Offset_EX),
    .Rx_Reg_2(Rx_Reg_EX), .Ry_Reg_2(Ry_Reg_EX), .Rz_Reg_2(Rz_Reg_EX), .OPCODE_2(OPCODE_EX),
    .Inc_PC_Reg_2(Inc_PC_Reg_EX));
  Comparator #(.width(32), .mode("unsigned")) comparator_1 (
    .a(Rx_Reg_EX), .b(Ry_Reg_EX), .eq(comparator_1_eq));  // open: gt, lt
  ROM #(.addrWidth(4), .dataWidth(6)) rom_2 (.addr(OPCODE_EX), .data({B_Selector, A_Selector, func}));  // open: sel
  Multiplexer #(.select(2), .width(32), .disabled(0), .enable("false")) multiplexer_8 (
    .in0(Ry_Reg_EX), .in1(Rx_Reg_EX), .out(multiplexer_8_out), .sel(A_Selector));  // open: in2, in3
  ALU alu_1 (.A(multiplexer_8_out), .B(multiplexer_9_out), .func(func), .ALU_Result(ALU_Result));
  Multiplexer #(.select(2), .width(32), .disabled(0), .enable("false")) multiplexer_9 (
    .in0(Rz_Reg_EX), .in1(Offset_EX), .in2(Ry_Reg_EX), .out(multiplexer_9_out), .sel(B_Selector));  // open: in3
  Adder #(.width(32)) adder_2 (.a(Inc_PC_Reg_EX), .b(Offset_EX), .out(PC___Offset_Ex));  // open: cin, cout
  Comparator #(.width(4), .mode("unsigned")) comparator_2 (
    .a(OPCODE_EX), .b(4'b0101), .eq(comparator_2_eq));  // open: gt, lt
  not not_3 (not_3_out, comparator_1_eq);
  Comparator #(.width(4), .mode("unsigned")) comparator_3 (
    .a(OPCODE_EX), .b(4'b0110), .eq(comparator_3_eq));  // open: gt, lt
  Comparator #(.width(4), .mode("unsigned")) comparator_4 (
    .a(OPCODE_EX), .b(4'b0111), .eq(comparator_4_eq));  // open: gt, lt
  and and_1 (and_1_out, comparator_2_eq, not_3_out);
  Comparator #(.width(32), .mode("unsigned")) comparator_5 (
    .a(Rx_Reg_EX), .b(Ry_Reg_EX), .eq(comparator_5_eq));  // open: gt, lt
  or or_2 (PC_Input_selector[0], and_1_out, comparator_4_eq);
  or or_3 (PC_Input_selector[1], comparator_3_eq, comparator_4_eq);
  Multiplexer #(.width(32), .disabled(0), .enable("false")) multiplexer_10 (
    .in0(Inc_PC_Reg_EX), .in1(PC___Offset_Ex), .out(multiplexer_10_out), .sel(and_2_out));
  and and_2 (and_2_out, not_4_out, 1'b1);
  not not_4 (not_4_out, comparator_5_eq);
  Multiplexer #(.select(2), .width(32), .disabled(0), .enable("false")) multiplexer_11 (
    .in0(ALU_Result), .in1(multiplexer_10_out), .in2(ALU_Result), .in3(ALU_Result), .out(multiplexer_11_out),
    .sel(func));
  EX_MEM_Buffer ex_mem_buffer_1 (
    .in_1(CLK), .Rx_Reg(Rx_Reg_EX), .OPCODE(OPCODE_EX), .ALU_reg(multiplexer_11_out), .in_2(1'b0),
    .in_4(1'b0), .Rx_Reg_2(Rx_Reg_MEM), .OPCODE_2(OPCODE_MEM), .ALU_Reg_2(ALU_Result_MEM),
    .Offset(Offset_EX), .Offset_Reg(Offset_MEM), .Inc_PC_Reg(Inc_PC_Reg_EX), .Inc_PC_Reg_2(Inc_PC_MEM),
    .Ry_Reg_EX(Ry_Reg_EX), .Ry_Reg_EX_2(Ry_Reg_MEM), .Rz_Reg_EX_2(Rz_Reg_MEM), .Rz_Reg_EX(Rz_Reg_EX));  // open: in_3
  Bit_Extender #(.in_width(32), .out_width(24), .\type ("sign")) bit_extender_5 (
    .in(ALU_Result_MEM), .out(bit_extender_5_out));
  Comparator #(.width(4), .mode("unsigned")) comparator_6 (
    .a(OPCODE_MEM), .b(4'b0100), .eq(comparator_6_eq));  // open: gt, lt
  Comparator #(.width(4), .mode("unsigned")) comparator_7 (
    .a(OPCODE_MEM), .b(4'b0011), .eq(comparator_7_eq));  // open: gt, lt
  RAM #(.addrWidth(24), .dataWidth(32), .bus("separate")) ram_2 (
    .addr(bit_extender_5_out), .din(Rz_Reg_MEM), .data(D_Mem_Out), .str(comparator_6_eq), .clk(CLK),
    .ld(comparator_7_eq));  // open: sel, clr
  MEM_WB_Buffer mem_wb_buffer_1 (
    .in_1(CLK), .Rx_Reg(Rx_Reg_MEM), .OPCODE(OPCODE_MEM), .ALU_reg(ALU_Result_MEM), .in_2(1'b0), .in_3(1'b0),
    .Rx_Reg_2(Rx_Reg_WB), .OPCODE_2(OPCODE_WB), .ALU_Reg_2(ALU_RESULT_WB), .Ry_Reg(Ry_Reg_MEM),
    .Rx_Reg_3(Ry_Reg_WB), .Inc_PC_Reg(Inc_PC_MEM), .Inc_PC_Reg_2(Inc_PC_WB), .D_MEM_OUT(D_Mem_Out),
    .D_MEM_OUT_2(D_Mem_Out_WB), .OFFSET(Offset_MEM), .OFFSET_2(Offset_WB));
  Adder #(.width(32)) adder_3 (.a(Inc_PC_WB), .b(Offset_WB), .out(adder_3_out));  // open: cin, cout
  Multiplexer #(.select(2), .width(32), .disabled(0), .enable("false")) multiplexer_12 (
    .in0(ALU_RESULT_WB), .in1(Inc_PC_WB), .in2(D_Mem_Out_WB), .in3(adder_3_out), .out(DPRF_Input),
    .sel(or_4_out));
  or or_4 (or_4_out[0], if_LEA, if_JALR);
  or or_5 (or_4_out[1], if_LW, if_LEA);
  Comparator #(.width(4), .mode("unsigned")) comparator_8 (.a(OPCODE_WB), .b(4'b0011), .eq(if_LW));  // open: gt, lt
  not not_5 (not_5_out, comparator_9_eq);
  Comparator #(.width(4), .mode("unsigned")) comparator_9 (
    .a(OPCODE_WB), .b(4'b0100), .eq(comparator_9_eq));  // open: gt, lt
  Comparator #(.width(4), .mode("unsigned")) comparator_10 (.a(OPCODE_WB), .b(4'b0110), .eq(if_JALR));  // open: gt, lt
  Comparator #(.width(4), .mode("unsigned")) comparator_11 (
    .a(OPCODE_WB), .b(4'b0101), .eq(comparator_11_eq));  // open: gt, lt
  not not_6 (not_6_out, comparator_11_eq);
  Comparator #(.width(4), .mode("unsigned")) comparator_12 (.a(OPCODE_WB), .b(4'b1001), .eq(if_LEA));  // open: gt, lt
  and and_3 (WREn, not_5_out, not_6_out);

  // Notes on the sheet:
  //   contents of rom_1 (hex, n*v repeats v):
  //   d d 15 15 16 16 5 0 d 11
  //   contents of rom_2 (hex, n*v repeats v):
  //   0 0 10 10 10 25 0 0 3
endmodule

module IF_IDRR_Buffer (
  input  in_1,
  input  in_2,
  input  in_3,
  input  [31:0] I_MEM_out,
  input  [31:0] Inc_PC,
  output [19:0] Offset,
  output [3:0] Rz,
  output [3:0] Ry,
  output [3:0] Rx,
  output [3:0] OPCODE,
  output [31:0] Inc_PC_Reg
);

  wire multiplexer_2_out, multiplexer_4_out;
  wire [31:0] multiplexer_1_out, multiplexer_3_out;

  Multiplexer #(.width(32), .disabled(0), .enable("false")) multiplexer_1 (
    .in0(I_MEM_out), .in1({32{1'b0}}), .out(multiplexer_1_out), .sel(in_2));
  Multiplexer #(.disabled(0), .enable("false")) multiplexer_2 (
    .in0(1'b1), .in1(1'b0), .out(multiplexer_2_out), .sel(in_3));
  Multiplexer #(.width(32), .disabled(0), .enable("false")) multiplexer_3 (
    .in0(Inc_PC), .in1({32{1'b0}}), .out(multiplexer_3_out), .sel(in_2));
  Multiplexer #(.disabled(0), .enable("false")) multiplexer_4 (
    .in0(1'b1), .in1(1'b0), .out(multiplexer_4_out), .sel(in_3));
  Register #(.width(32)) I_MEM_reg (
    .D(multiplexer_1_out), .en(multiplexer_2_out), .Q({OPCODE, Rx, Ry, Offset}), .clk(in_1));  // open: clr
  Register #(.width(32)) u_Inc_PC_reg (
    .D(multiplexer_3_out), .en(multiplexer_4_out), .Q(Inc_PC_Reg), .clk(in_1));  // open: clr

  assign Rz = Offset[3:0];

  // Other names for the same wires on the sheet: CLK = in_1; NOP = in_2; STALL = in_3
endmodule

module Dual_Ported_Register_File (
  input  CLK,
  input  WrEN,
  input  [3:0] WrREGNO,
  input  [3:0] RdREGNO1,
  input  [3:0] RdREGNO2,
  input  [31:0] INPUT,
  output [31:0] OUT1,
  output [31:0] OUT2
);

  wire En_a0, En_a1, En_a2, En_at, En_fp, En_k0, En_ra, En_s0, En_s1, En_s2, En_sp, En_t0, En_t1, En_t2,
       En_v0;
  wire [31:0] a0, a1, a2, at, fp, k0, ra, s0, s1, s2, sp, t0, t1, t2, v0, zero;

  Decoder #(.select(4), .disabled(0)) decoder_1 (
    .out1(En_at), .out2(En_v0), .out3(En_a0), .out4(En_a1), .out5(En_a2), .out6(En_t0), .out7(En_t1),
    .out8(En_t2), .out9(En_s0), .out10(En_s1), .out11(En_s2), .out12(En_k0), .out13(En_sp), .out14(En_fp),
    .out15(En_ra), .sel(WrREGNO), .en(WrEN));  // open: out0
  Register #(.width(32)) u_zero (.D(INPUT), .en(1'b0), .Q(zero), .clk(CLK));  // open: clr
  Register #(.width(32)) u_at (.D(INPUT), .en(En_at), .Q(at), .clk(CLK));  // open: clr
  Register #(.width(32)) u_v0 (.D(INPUT), .en(En_v0), .Q(v0), .clk(CLK));  // open: clr
  Register #(.width(32)) u_a0 (.D(INPUT), .en(En_a0), .Q(a0), .clk(CLK));  // open: clr
  Register #(.width(32)) u_a1 (.D(INPUT), .en(En_a1), .Q(a1), .clk(CLK));  // open: clr
  Register #(.width(32)) u_a2 (.D(INPUT), .en(En_a2), .Q(a2), .clk(CLK));  // open: clr
  Register #(.width(32)) u_t0 (.D(INPUT), .en(En_t0), .Q(t0), .clk(CLK));  // open: clr
  Register #(.width(32)) u_t1 (.D(INPUT), .en(En_t1), .Q(t1), .clk(CLK));  // open: clr
  Multiplexer #(.select(4), .width(32), .disabled(0), .enable("false")) multiplexer_1 (
    .in0(zero), .in1(at), .in2(v0), .in3(a0), .in4(a1), .in5(a2), .in6(t0), .in7(t1), .in8(t2), .in9(s0),
    .in10(s1), .in11(s2), .in12(k0), .in13(sp), .in14(fp), .in15(ra), .out(OUT2), .sel(RdREGNO2));
  Register #(.width(32)) u_t2 (.D(INPUT), .en(En_t2), .Q(t2), .clk(CLK));  // open: clr
  Register #(.width(32)) u_s0 (.D(INPUT), .en(En_s0), .Q(s0), .clk(CLK));  // open: clr
  Register #(.width(32)) u_s1 (.D(INPUT), .en(En_s1), .Q(s1), .clk(CLK));  // open: clr
  Register #(.width(32)) u_s2 (.D(INPUT), .en(En_s2), .Q(s2), .clk(CLK));  // open: clr
  Register #(.width(32)) u_k0 (.D(INPUT), .en(En_k0), .Q(k0), .clk(CLK));  // open: clr
  Register #(.width(32)) u_sp (.D(INPUT), .en(En_sp), .Q(sp), .clk(CLK));  // open: clr
  Register #(.width(32)) u_fp (.D(INPUT), .en(En_fp), .Q(fp), .clk(CLK));  // open: clr
  Register #(.width(32)) u_ra (.D(INPUT), .en(En_ra), .Q(ra), .clk(CLK));  // open: clr
  Multiplexer #(.select(4), .width(32), .disabled(0), .enable("false")) multiplexer_2 (
    .in0(zero), .in1(at), .in2(v0), .in3(a0), .in4(a1), .in5(a2), .in6(t0), .in7(t1), .in8(t2), .in9(s0),
    .in10(s1), .in11(s2), .in12(k0), .in13(sp), .in14(fp), .in15(ra), .out(OUT1), .sel(RdREGNO1));

  // Notes on the sheet:
  //   MODIFY AT YOUR OWN RISK
endmodule

module IDRR_EX_Buffer (
  input  CLK,
  input  in_2,
  input  in_3,
  input  [31:0] Offset,
  input  [31:0] Rx_Reg,
  input  [31:0] Ry_Reg,
  input  [31:0] Rz_Reg,
  input  [3:0] OPCODE,
  input  [31:0] Inc_PC_Reg,
  output [31:0] Offset_Reg,
  output [31:0] Rx_Reg_2,
  output [31:0] Ry_Reg_2,
  output [31:0] Rz_Reg_2,
  output [3:0] OPCODE_2,
  output [31:0] Inc_PC_Reg_2
);

  wire multiplexer_7_out, multiplexer_8_out, multiplexer_9_out, multiplexer_10_out, multiplexer_11_out,
       multiplexer_12_out;
  wire [3:0] multiplexer_5_out;
  wire [31:0] multiplexer_1_out, multiplexer_2_out, multiplexer_3_out, multiplexer_4_out, multiplexer_6_out;

  Pull_Resistor pull_resistor_1 (.node(in_3));
  Pull_Resistor pull_resistor_2 (.node(in_2));
  Multiplexer #(.width(32), .disabled(0), .enable("false")) multiplexer_1 (
    .in0(Offset), .in1({32{1'b0}}), .out(multiplexer_1_out), .sel(in_2));
  Multiplexer #(.width(32), .disabled(0), .enable("false")) multiplexer_2 (
    .in0(Rx_Reg), .in1({32{1'b0}}), .out(multiplexer_2_out), .sel(in_2));
  Multiplexer #(.width(32), .disabled(0), .enable("false")) multiplexer_3 (
    .in0(Ry_Reg), .in1({32{1'b0}}), .out(multiplexer_3_out), .sel(in_2));
  Multiplexer #(.width(32), .disabled(0), .enable("false")) multiplexer_4 (
    .in0(Rz_Reg), .in1({32{1'b0}}), .out(multiplexer_4_out), .sel(in_2));
  Multiplexer #(.width(4), .disabled(0), .enable("false")) multiplexer_5 (
    .in0(OPCODE), .in1(4'b0000), .out(multiplexer_5_out), .sel(in_2));
  Multiplexer #(.width(32), .disabled(0), .enable("false")) multiplexer_6 (
    .in0(Inc_PC_Reg), .in1({32{1'b0}}), .out(multiplexer_6_out), .sel(in_2));
  Multiplexer #(.disabled(0), .enable("false")) multiplexer_7 (
    .in0(1'b1), .in1(1'b0), .out(multiplexer_7_out), .sel(in_3));
  Register #(.width(32)) u_Offset_Reg (
    .D(multiplexer_1_out), .en(multiplexer_8_out), .Q(Offset_Reg), .clk(CLK));  // open: clr
  Multiplexer #(.disabled(0), .enable("false")) multiplexer_8 (
    .in0(1'b1), .in1(1'b0), .out(multiplexer_8_out), .sel(in_3));
  Register #(.width(32)) u_Rx_Reg (
    .D(multiplexer_2_out), .en(multiplexer_9_out), .Q(Rx_Reg_2), .clk(CLK));  // open: clr
  Multiplexer #(.disabled(0), .enable("false")) multiplexer_9 (
    .in0(1'b1), .in1(1'b0), .out(multiplexer_9_out), .sel(in_3));
  Register #(.width(32)) u_Ry_Reg (
    .D(multiplexer_3_out), .en(multiplexer_10_out), .Q(Ry_Reg_2), .clk(CLK));  // open: clr
  Multiplexer #(.disabled(0), .enable("false")) multiplexer_10 (
    .in0(1'b1), .in1(1'b0), .out(multiplexer_10_out), .sel(in_3));
  Register #(.width(32)) u_Rz_Reg (
    .D(multiplexer_4_out), .en(multiplexer_11_out), .Q(Rz_Reg_2), .clk(CLK));  // open: clr
  Multiplexer #(.disabled(0), .enable("false")) multiplexer_11 (
    .in0(1'b1), .in1(1'b0), .out(multiplexer_11_out), .sel(in_3));
  Register #(.width(4)) u_OPCODE (
    .D(multiplexer_5_out), .en(multiplexer_12_out), .Q(OPCODE_2), .clk(CLK));  // open: clr
  Multiplexer #(.disabled(0), .enable("false")) multiplexer_12 (
    .in0(1'b1), .in1(1'b0), .out(multiplexer_12_out), .sel(in_3));
  Register #(.width(32)) u_Inc_PC_Reg (
    .D(multiplexer_6_out), .en(multiplexer_7_out), .Q(Inc_PC_Reg_2), .clk(CLK));  // open: clr

  // Other names for the same wires on the sheet: NOP = in_2; STALL = in_3
endmodule

module EX_MEM_Buffer (
  input  in_1,
  input  in_2,
  input  in_3,
  input  in_4,
  input  [31:0] Rx_Reg,
  input  [3:0] OPCODE,
  input  [31:0] ALU_reg,
  input  [31:0] Offset,
  input  [31:0] Inc_PC_Reg,
  input  [31:0] Ry_Reg_EX,
  input  [31:0] Rz_Reg_EX,
  output [31:0] Rx_Reg_2,
  output [3:0] OPCODE_2,
  output [31:0] ALU_Reg_2,
  output [31:0] Offset_Reg,
  output [31:0] Inc_PC_Reg_2,
  output [31:0] Ry_Reg_EX_2,
  output [31:0] Rz_Reg_EX_2
);

  wire multiplexer_4_out, multiplexer_8_out, multiplexer_9_out, multiplexer_10_out, multiplexer_12_out,
       multiplexer_13_out, multiplexer_14_out;
  wire [3:0] multiplexer_2_out;
  wire [31:0] multiplexer_1_out, multiplexer_3_out, multiplexer_5_out, multiplexer_6_out, multiplexer_7_out,
       multiplexer_11_out;

  Multiplexer #(.width(32), .disabled(0), .enable("false")) multiplexer_1 (
    .in0(Rx_Reg), .in1({32{1'b0}}), .out(multiplexer_1_out), .sel(in_2));
  Multiplexer #(.width(4), .disabled(0), .enable("false")) multiplexer_2 (
    .in0(OPCODE), .in1(4'b0000), .out(multiplexer_2_out), .sel(in_2));
  Multiplexer #(.width(32), .disabled(0), .enable("false")) multiplexer_3 (
    .in0(ALU_reg), .in1({32{1'b0}}), .out(multiplexer_3_out), .sel(in_2));
  Multiplexer #(.disabled(0), .enable("false")) multiplexer_4 (
    .in0(1'b1), .in1(1'b0), .out(multiplexer_4_out), .sel(in_4));
  Multiplexer #(.width(32), .disabled(0), .enable("false")) multiplexer_5 (
    .in0(Offset), .in1({32{1'b0}}), .out(multiplexer_5_out), .sel(in_2));
  Multiplexer #(.width(32), .disabled(0), .enable("false")) multiplexer_6 (
    .in0(Ry_Reg_EX), .in1({32{1'b0}}), .out(multiplexer_6_out), .sel(in_2));
  Multiplexer #(.width(32), .disabled(0), .enable("false")) multiplexer_7 (
    .in0(Rz_Reg_EX), .in1({32{1'b0}}), .out(multiplexer_7_out), .sel(in_2));
  Multiplexer #(.disabled(0), .enable("false")) multiplexer_8 (
    .in0(1'b1), .in1(1'b0), .out(multiplexer_8_out), .sel(in_4));
  Register #(.width(4)) u_OPCODE (
    .D(multiplexer_2_out), .en(multiplexer_9_out), .Q(OPCODE_2), .clk(in_1));  // open: clr
  Multiplexer #(.disabled(0), .enable("false")) multiplexer_9 (
    .in0(1'b1), .in1(1'b0), .out(multiplexer_9_out), .sel(in_4));
  Register #(.width(32)) u_ALU_Reg (
    .D(multiplexer_3_out), .en(multiplexer_4_out), .Q(ALU_Reg_2), .clk(in_1));  // open: clr
  Multiplexer #(.disabled(0), .enable("false")) multiplexer_10 (
    .in0(1'b1), .in1(1'b0), .out(multiplexer_10_out), .sel(in_4));
  Multiplexer #(.width(32), .disabled(0), .enable("false")) multiplexer_11 (
    .in0(Inc_PC_Reg), .in1({32{1'b0}}), .out(multiplexer_11_out), .sel(in_2));
  Multiplexer #(.disabled(0), .enable("false")) multiplexer_12 (
    .in0(1'b1), .in1(1'b0), .out(multiplexer_12_out), .sel(in_4));
  Multiplexer #(.disabled(0), .enable("false")) multiplexer_13 (
    .in0(1'b1), .in1(1'b0), .out(multiplexer_13_out), .sel(in_4));
  Register #(.width(32)) Rz_Reg (
    .D(multiplexer_7_out), .en(multiplexer_14_out), .Q(Rz_Reg_EX_2), .clk(in_1));  // open: clr
  Multiplexer #(.disabled(0), .enable("false")) multiplexer_14 (
    .in0(1'b1), .in1(1'b0), .out(multiplexer_14_out), .sel(in_4));
  Register #(.width(32)) u_Rx_Reg (
    .D(multiplexer_1_out), .en(multiplexer_8_out), .Q(Rx_Reg_2), .clk(in_1));  // open: clr
  Register #(.width(32)) u_Offset_Reg (
    .D(multiplexer_5_out), .en(multiplexer_10_out), .Q(Offset_Reg), .clk(in_1));  // open: clr
  Register #(.width(32)) u_Inc_PC_Reg (
    .D(multiplexer_11_out), .en(multiplexer_12_out), .Q(Inc_PC_Reg_2), .clk(in_1));  // open: clr
  Register #(.width(32)) Rz_Reg_2 (
    .D(multiplexer_6_out), .en(multiplexer_13_out), .Q(Ry_Reg_EX_2), .clk(in_1));  // open: clr

  // Other names for the same wires on the sheet: CLK = in_1; NOP = in_2; RESET = in_3; STALL = in_4
endmodule

module MEM_WB_Buffer (
  input  in_1,
  input  in_2,
  input  in_3,
  input  [31:0] Rx_Reg,
  input  [3:0] OPCODE,
  input  [31:0] ALU_reg,
  input  [31:0] Ry_Reg,
  input  [31:0] Inc_PC_Reg,
  input  [31:0] D_MEM_OUT,
  input  [31:0] OFFSET,
  output [31:0] Rx_Reg_2,
  output [3:0] OPCODE_2,
  output [31:0] ALU_Reg_2,
  output [31:0] Rx_Reg_3,
  output [31:0] Inc_PC_Reg_2,
  output [31:0] D_MEM_OUT_2,
  output [31:0] OFFSET_2
);

  wire multiplexer_4_out, multiplexer_6_out, multiplexer_7_out, multiplexer_8_out, multiplexer_10_out,
       multiplexer_12_out, multiplexer_14_out;
  wire [3:0] multiplexer_2_out;
  wire [31:0] multiplexer_1_out, multiplexer_3_out, multiplexer_5_out, multiplexer_9_out, multiplexer_11_out,
       multiplexer_13_out;

  Multiplexer #(.width(32), .disabled(0), .enable("false")) multiplexer_1 (
    .in0(Rx_Reg), .in1({32{1'b0}}), .out(multiplexer_1_out), .sel(in_2));
  Multiplexer #(.width(4), .disabled(0), .enable("false")) multiplexer_2 (
    .in0(OPCODE), .in1(4'b0000), .out(multiplexer_2_out), .sel(in_2));
  Multiplexer #(.width(32), .disabled(0), .enable("false")) multiplexer_3 (
    .in0(ALU_reg), .in1({32{1'b0}}), .out(multiplexer_3_out), .sel(in_2));
  Multiplexer #(.disabled(0), .enable("false")) multiplexer_4 (
    .in0(1'b1), .in1(1'b0), .out(multiplexer_4_out), .sel(in_3));
  Multiplexer #(.width(32), .disabled(0), .enable("false")) multiplexer_5 (
    .in0(Ry_Reg), .in1({32{1'b0}}), .out(multiplexer_5_out), .sel(in_2));
  Multiplexer #(.disabled(0), .enable("false")) multiplexer_6 (
    .in0(1'b1), .in1(1'b0), .out(multiplexer_6_out), .sel(in_3));
  Register #(.width(4)) u_OPCODE (
    .D(multiplexer_2_out), .en(multiplexer_7_out), .Q(OPCODE_2), .clk(in_1));  // open: clr
  Multiplexer #(.disabled(0), .enable("false")) multiplexer_7 (
    .in0(1'b1), .in1(1'b0), .out(multiplexer_7_out), .sel(in_3));
  Register #(.width(32)) u_ALU_Reg (
    .D(multiplexer_3_out), .en(multiplexer_4_out), .Q(ALU_Reg_2), .clk(in_1));  // open: clr
  Multiplexer #(.disabled(0), .enable("false")) multiplexer_8 (
    .in0(1'b1), .in1(1'b0), .out(multiplexer_8_out), .sel(in_3));
  Multiplexer #(.width(32), .disabled(0), .enable("false")) multiplexer_9 (
    .in0(Inc_PC_Reg), .in1({32{1'b0}}), .out(multiplexer_9_out), .sel(in_2));
  Multiplexer #(.disabled(0), .enable("false")) multiplexer_10 (
    .in0(1'b1), .in1(1'b0), .out(multiplexer_10_out), .sel(in_3));
  Multiplexer #(.width(32), .disabled(0), .enable("false")) multiplexer_11 (
    .in0(D_MEM_OUT), .in1({32{1'b0}}), .out(multiplexer_11_out), .sel(in_2));
  Multiplexer #(.disabled(0), .enable("false")) multiplexer_12 (
    .in0(1'b1), .in1(1'b0), .out(multiplexer_12_out), .sel(in_3));
  Multiplexer #(.width(32), .disabled(0), .enable("false")) multiplexer_13 (
    .in0(OFFSET), .in1({32{1'b0}}), .out(multiplexer_13_out), .sel(in_2));
  Multiplexer #(.disabled(0), .enable("false")) multiplexer_14 (
    .in0(1'b1), .in1(1'b0), .out(multiplexer_14_out), .sel(in_3));
  Register #(.width(32)) u_Rx_Reg (
    .D(multiplexer_1_out), .en(multiplexer_6_out), .Q(Rx_Reg_2), .clk(in_1));  // open: clr
  Register #(.width(32)) u_Rx_Reg_2 (
    .D(multiplexer_5_out), .en(multiplexer_8_out), .Q(Rx_Reg_3), .clk(in_1));  // open: clr
  Register #(.width(32)) u_Inc_PC_Reg (
    .D(multiplexer_9_out), .en(multiplexer_10_out), .Q(Inc_PC_Reg_2), .clk(in_1));  // open: clr
  Register #(.width(32)) u_D_MEM_OUT (
    .D(multiplexer_11_out), .en(multiplexer_12_out), .Q(D_MEM_OUT_2), .clk(in_1));  // open: clr
  Register #(.width(32)) u_OFFSET (
    .D(multiplexer_13_out), .en(multiplexer_14_out), .Q(OFFSET_2), .clk(in_1));  // open: clr

  // Other names for the same wires on the sheet: CLK = in_1; NOP = in_2; STALL = in_3
endmodule

module ALU (
  input  [31:0] A,
  input  [31:0] B,
  input  [1:0] func,
  output [31:0] ALU_Result
);

  wire comparator_1_eq, comparator_2_lt, not_1_out;
  wire [31:0] adder_1_out, bit_extender_1_out, bit_extender_2_out, nand_1_out;

  Comparator #(.width(32), .mode("unsigned")) comparator_1 (.a(A), .b(B), .eq(comparator_1_eq));  // open: gt, lt
  Comparator #(.width(32), .mode("unsigned")) comparator_2 (.a(A), .b(B), .lt(comparator_2_lt));  // open: gt, eq
  not not_1 (not_1_out, comparator_1_eq);
  Adder #(.width(32)) adder_1 (.a(A), .b(B), .out(adder_1_out));  // open: cin, cout
  assign bit_extender_1_out = {{31{not_1_out}}, not_1_out};  // Bit_Extender bit_extender_1
  assign nand_1_out = ~(A & B);  // NAND_Gate nand_1, 32 bits wide
  assign bit_extender_2_out = {{31{comparator_2_lt}}, comparator_2_lt};  // Bit_Extender bit_extender_2
  Multiplexer #(.select(2), .width(32), .disabled(0), .enable("false")) multiplexer_1 (
    .in0(adder_1_out), .in1(bit_extender_1_out), .in2(nand_1_out), .in3(bit_extender_2_out),
    .out(ALU_Result), .sel(func));
endmodule

module Stall_Handler (
  input  [3:0] OPCODE_EX,
  input  [3:0] OPCODE_MEM,
  input  [31:0] RX_EX,
  input  [3:0] OPCODE_WB,
  input  [3:0] DPRF_IN0,
  input  [31:0] RX_MEM,
  input  [3:0] DPRF_IN2,
  input  [31:0] RX_WB,
  output STALL
);

  wire and_1_out, and_2_out, and_3_out, and_4_out, and_5_out, and_6_out, and_7_out, and_8_out, and_9_out,
       comparator_1_eq, comparator_2_eq, comparator_3_eq, comparator_4_eq, comparator_5_eq, comparator_6_eq,
       comparator_7_eq, comparator_8_eq, comparator_9_eq, comparator_10_eq, comparator_11_eq,
       comparator_12_eq, comparator_13_eq, comparator_14_eq, comparator_15_eq, comparator_16_eq,
       comparator_17_eq, comparator_18_eq, comparator_19_eq, comparator_20_eq, comparator_21_eq,
       comparator_22_eq, comparator_23_eq, comparator_24_eq, comparator_25_eq, comparator_26_eq,
       comparator_27_eq, comparator_28_eq, comparator_29_eq, comparator_30_eq, or_1_out, or_2_out, or_3_out,
       or_4_out, or_5_out, or_6_out;
  wire [31:0] DPRF_IN0_t, DPRF_IN1;

  assign DPRF_IN0_t = {{28{DPRF_IN0[3]}}, DPRF_IN0};  // Bit_Extender bit_extender_1
  assign DPRF_IN1 = {{28{DPRF_IN2[3]}}, DPRF_IN2};  // Bit_Extender bit_extender_2
  Comparator #(.width(4), .mode("unsigned")) comparator_1 (
    .a(OPCODE_EX), .b(4'b0001), .eq(comparator_1_eq));  // open: gt, lt
  Comparator #(.width(4), .mode("unsigned")) comparator_2 (
    .a(OPCODE_EX), .b(4'b0010), .eq(comparator_2_eq));  // open: gt, lt
  Comparator #(.width(4), .mode("unsigned")) comparator_3 (
    .a(OPCODE_EX), .b(4'b0011), .eq(comparator_3_eq));  // open: gt, lt
  Comparator #(.width(4), .mode("unsigned")) comparator_4 (
    .a(OPCODE_EX), .b(4'b0110), .eq(comparator_4_eq));  // open: gt, lt
  Comparator #(.width(4), .mode("unsigned")) comparator_5 (
    .a(OPCODE_EX), .b(4'b1000), .eq(comparator_5_eq));  // open: gt, lt
  Comparator #(.width(4), .mode("unsigned")) comparator_6 (
    .a(OPCODE_EX), .b(4'b1001), .eq(comparator_6_eq));  // open: gt, lt
  Comparator #(.width(32), .mode("unsigned")) comparator_7 (
    .a(RX_EX), .b(DPRF_IN0_t), .eq(comparator_7_eq));  // open: gt, lt
  Comparator #(.width(32), .mode("unsigned")) comparator_8 (
    .a(DPRF_IN0_t), .b({32{1'b0}}), .eq(comparator_8_eq));  // open: gt, lt
  Comparator #(.width(32), .mode("unsigned")) comparator_9 (
    .a(RX_EX), .b(DPRF_IN1), .eq(comparator_9_eq));  // open: gt, lt
  Comparator #(.width(32), .mode("unsigned")) comparator_10 (
    .a(DPRF_IN1), .b({32{1'b0}}), .eq(comparator_10_eq));  // open: gt, lt
  Comparator #(.width(4), .mode("unsigned")) comparator_11 (
    .a(OPCODE_MEM), .b(4'b0001), .eq(comparator_11_eq));  // open: gt, lt
  Comparator #(.width(4), .mode("unsigned")) comparator_12 (
    .a(OPCODE_MEM), .b(4'b0010), .eq(comparator_12_eq));  // open: gt, lt
  Comparator #(.width(4), .mode("unsigned")) comparator_13 (
    .a(OPCODE_MEM), .b(4'b0011), .eq(comparator_13_eq));  // open: gt, lt
  Comparator #(.width(4), .mode("unsigned")) comparator_14 (
    .a(OPCODE_MEM), .b(4'b0110), .eq(comparator_14_eq));  // open: gt, lt
  Comparator #(.width(4), .mode("unsigned")) comparator_15 (
    .a(OPCODE_MEM), .b(4'b1000), .eq(comparator_15_eq));  // open: gt, lt
  Comparator #(.width(4), .mode("unsigned")) comparator_16 (
    .a(OPCODE_MEM), .b(4'b1001), .eq(comparator_16_eq));  // open: gt, lt
  Comparator #(.width(32), .mode("unsigned")) comparator_17 (
    .a(RX_MEM), .b(DPRF_IN0_t), .eq(comparator_17_eq));  // open: gt, lt
  Comparator #(.width(32), .mode("unsigned")) comparator_18 (
    .a(DPRF_IN0_t), .b({32{1'b0}}), .eq(comparator_18_eq));  // open: gt, lt
  Comparator #(.width(32), .mode("unsigned")) comparator_19 (
    .a(RX_MEM), .b(DPRF_IN1), .eq(comparator_19_eq));  // open: gt, lt
  Comparator #(.width(32), .mode("unsigned")) comparator_20 (
    .a(DPRF_IN1), .b({32{1'b0}}), .eq(comparator_20_eq));  // open: gt, lt
  Comparator #(.width(4), .mode("unsigned")) comparator_21 (
    .a(OPCODE_WB), .b(4'b0001), .eq(comparator_21_eq));  // open: gt, lt
  Comparator #(.width(4), .mode("unsigned")) comparator_22 (
    .a(OPCODE_WB), .b(4'b0010), .eq(comparator_22_eq));  // open: gt, lt
  Comparator #(.width(4), .mode("unsigned")) comparator_23 (
    .a(OPCODE_WB), .b(4'b0011), .eq(comparator_23_eq));  // open: gt, lt
  Comparator #(.width(4), .mode("unsigned")) comparator_24 (
    .a(OPCODE_WB), .b(4'b0110), .eq(comparator_24_eq));  // open: gt, lt
  Comparator #(.width(4), .mode("unsigned")) comparator_25 (
    .a(OPCODE_WB), .b(4'b1000), .eq(comparator_25_eq));  // open: gt, lt
  Comparator #(.width(4), .mode("unsigned")) comparator_26 (
    .a(OPCODE_WB), .b(4'b1001), .eq(comparator_26_eq));  // open: gt, lt
  Comparator #(.width(32), .mode("unsigned")) comparator_27 (
    .a(RX_WB), .b(DPRF_IN0_t), .eq(comparator_27_eq));  // open: gt, lt
  Comparator #(.width(32), .mode("unsigned")) comparator_28 (
    .a(DPRF_IN0_t), .b({32{1'b0}}), .eq(comparator_28_eq));  // open: gt, lt
  Comparator #(.width(32), .mode("unsigned")) comparator_29 (
    .a(RX_WB), .b(DPRF_IN1), .eq(comparator_29_eq));  // open: gt, lt
  Comparator #(.width(32), .mode("unsigned")) comparator_30 (
    .a(DPRF_IN1), .b({32{1'b0}}), .eq(comparator_30_eq));  // open: gt, lt
  and and_1 (and_1_out, comparator_7_eq, ~comparator_8_eq);  // AND_Gate
  and and_2 (and_2_out, comparator_9_eq, ~comparator_10_eq);  // AND_Gate
  and and_3 (and_3_out, comparator_17_eq, ~comparator_18_eq);  // AND_Gate
  and and_4 (and_4_out, comparator_19_eq, ~comparator_20_eq);  // AND_Gate
  and and_5 (and_5_out, comparator_27_eq, ~comparator_28_eq);  // AND_Gate
  and and_6 (and_6_out, comparator_29_eq, ~comparator_30_eq);  // AND_Gate
  or or_1 (or_1_out, comparator_1_eq, comparator_2_eq, comparator_3_eq, comparator_4_eq, comparator_5_eq, comparator_6_eq);
  or or_2 (or_2_out, and_1_out, and_2_out);
  or or_3 (or_3_out, comparator_11_eq, comparator_12_eq, comparator_13_eq, comparator_14_eq, comparator_15_eq, comparator_16_eq);
  or or_4 (or_4_out, and_3_out, and_4_out);
  or or_5 (or_5_out, comparator_21_eq, comparator_22_eq, comparator_23_eq, comparator_24_eq, comparator_25_eq, comparator_26_eq);
  or or_6 (or_6_out, and_5_out, and_6_out);
  and and_7 (and_7_out, or_1_out, or_2_out);
  and and_8 (and_8_out, or_3_out, or_4_out);
  and and_9 (and_9_out, or_5_out, or_6_out);
  or or_7 (STALL, and_7_out, and_8_out, and_9_out);
endmodule
